// Logisim project logoGuara.circ as structural Verilog: 4 circuits, main circuit main
module main (
  input  in_1,
  output [7:0] out_2
);

  wire clock_1_out, ula_1_escrevepc;
  wire [3:0] Op, rom_1_data;
  wire [7:0] adder_1_out, bancoderegistradores_1_readdata1, bancoderegistradores_1_readdata2,
       bancoderegistradores_1_reg0out, multiplexer_1_out, PC;

  Register u_PC (.D(multiplexer_1_out), .en(1'b1), .clk(clock_1_out), .Q(PC), .clr(in_1));
  Clock clock_1 (.out(clock_1_out));
  Multiplexer #(.width(8), .enable("false")) multiplexer_1 (
    .in0(adder_1_out), .in1(out_2), .out(multiplexer_1_out), .sel(ula_1_escrevepc));
  Adder adder_1 (.a(8'h1), .b(PC), .out(adder_1_out));  // open: cin, cout
  ROM rom_1 (.addr(PC), .data({Op, rom_1_data}));
  bancoDeRegistradores bancoderegistradores_1 (
    .ReadRegister1(rom_1_data[1:0]), .ReadRegister2(rom_1_data[3:2]),
    .Reg0Out(bancoderegistradores_1_reg0out), .ReadData1(bancoderegistradores_1_readdata1),
    .ReadData2(bancoderegistradores_1_readdata2));  // open: WriteData, WriteRegister, RegWrite, CLOCK, CLEAR
  ULA ula_1 (
    .A(bancoderegistradores_1_readdata1), .B(bancoderegistradores_1_readdata2), .Funcao(Op),
    .Reg0(bancoderegistradores_1_reg0out), .PC(PC), .Resultado(out_2), .EscrevePc(ula_1_escrevepc));
endmodule

module bancoDeRegistradores (
  input  [1:0] ReadRegister1,
  input  [1:0] ReadRegister2,
  input  [7:0] WriteData,
  input  [1:0] WriteRegister,
  input  RegWrite,
  input  CLOCK,
  input  CLEAR,
  output [7:0] Reg0Out,
  output [7:0] ReadData1,
  output [7:0] ReadData2
);

  wire WE0, WE1, WE2, WE3;
  wire [7:0] Reg0In, Reg1In, Reg1Out, Reg2In, Reg2Out, Reg3In, Reg3Out;

  Demultiplexer #(.select(2), .width(8), .disabled("Z")) demultiplexer_1 (
    .out0(Reg0In), .out1(Reg1In), .out2(Reg2In), .out3(Reg3In), .in(WriteData), .sel(WriteRegister));  // open: en
  Demultiplexer #(.select(2), .disabled("Z")) demultiplexer_2 (
    .out0(WE0), .out1(WE1), .out2(WE2), .out3(WE3), .in(RegWrite), .sel(WriteRegister));  // open: en
  Register Reg0 (.D(Reg0In), .en(WE0), .clk(CLOCK), .Q(Reg0Out), .clr(CLEAR));
  Register Reg1 (.D(Reg1In), .en(WE1), .clk(CLOCK), .Q(Reg1Out), .clr(CLEAR));
  Register Reg2 (.D(Reg2In), .en(WE2), .clk(CLOCK), .Q(Reg2Out), .clr(CLEAR));
  Register Reg3 (.D(Reg3In), .en(WE3), .clk(CLOCK), .Q(Reg3Out), .clr(CLEAR));
  Multiplexer #(.select(2), .width(8), .disabled("Z"), .enable("false")) multiplexer_1 (
    .in0(Reg0Out), .in1(Reg1Out), .in2(Reg2Out), .in3(Reg3Out), .out(ReadData1), .sel(ReadRegister1));
  Multiplexer #(.select(2), .width(8), .disabled("Z"), .enable("false")) multiplexer_2 (
    .in0(Reg0Out), .in1(Reg1Out), .in2(Reg2Out), .in3(Reg3Out), .out(ReadData2), .sel(ReadRegister2));
endmodule

module ULA (
  input  [7:0] A,
  input  [7:0] B,
  input  [3:0] Funcao,
  input  [7:0] Reg0,
  input  [7:0] PC,
  output [7:0] Resultado,
  output EscrevePc
);

  wire BrziEscrevePc, BrzrEscrevePc;
  wire [2:0] bit_extender_3_out, bit_extender_4_out;
  wire [7:0] AAddIn, AAndIn, ABrzrIn, adder_1_out, AddOut, AIdIn, AMovhIn, AMovlIn, AndOut, AOrIn, ASlrIn,
       ASrrIn, AStIn, ASubIn, BAddIn, BAndIn, BBrziIn, BBrzrIn, BIdIn, bit_extender_1_out,
       bit_extender_2_out, BJiIn, BJrIn, BMovhIn, BMovlIn, BMovrIn, BNotIn, BOrIn, BrziOut, BrzrOut, BSlrIn,
       BSrrIn, BStIn, BSubIn, IdOut, JiOut, MovhOut, MovlOut, NotOut, OrOut, SlrOut, SrrOut, StOut, SubOut;

  Demultiplexer #(.select(4), .width(8), .enable("false")) demultiplexer_1 (
    .out0(ABrzrIn), .out4(AIdIn), .out5(AStIn), .out7(AMovhIn), .out8(AMovlIn), .out9(AAddIn),
    .out10(ASubIn), .out11(AAndIn), .out12(AOrIn), .out14(ASlrIn), .out15(ASrrIn), .in(A), .sel(Funcao));  // open: out1, out2, out3, out6, out13
  Demultiplexer #(.select(4), .width(8), .enable("false")) demultiplexer_2 (
    .out0(BBrzrIn), .out1(BBrziIn), .out2(BJrIn), .out3(BJiIn), .out4(BIdIn), .out5(BStIn), .out6(BMovrIn),
    .out7(BMovhIn), .out8(BMovlIn), .out9(BAddIn), .out10(BSubIn), .out11(BAndIn), .out12(BOrIn),
    .out13(BNotIn), .out14(BSlrIn), .out15(BSrrIn), .in(B), .sel(Funcao));
  Multiplexer #(.select(4), .width(8), .enable("false")) multiplexer_1 (
    .in0(BrzrOut), .in1(BrziOut), .in2(BJrIn), .in3(JiOut), .in4(IdOut), .in5(StOut), .in6(BMovrIn),
    .in7(MovhOut), .in8(MovlOut), .in9(AddOut), .in10(SubOut), .in11(AndOut), .in12(OrOut), .in13(NotOut),
    .in14(SlrOut), .in15(SrrOut), .out(Resultado), .sel(Funcao));
  Comparator comparator_1 (.a(ABrzrIn), .b({8{1'b0}}), .eq(BrzrEscrevePc));  // open: gt, lt
  Adder adder_1 (.a(BBrziIn), .b(PC), .out(adder_1_out));  // open: cin, cout
  Comparator comparator_2 (.a(Reg0), .b({8{1'b0}}), .eq(BrziEscrevePc));  // open: gt, lt
  Adder adder_2 (.a(BJiIn), .b(PC), .out(JiOut));  // open: cin, cout
  assign bit_extender_1_out = {{4{Reg0[3]}}, Reg0[3:0]};  // Bit_Extender bit_extender_1
  assign bit_extender_2_out = {{4{Reg0[7]}}, Reg0[7:4]};  // Bit_Extender bit_extender_2
  Adder adder_3 (.a(AAddIn), .b(BAddIn), .out(AddOut));  // open: cin, cout
  Subtractor subtractor_1 (.a(ASubIn), .b(BSubIn), .out(SubOut));  // open: bin, bout
  assign AndOut = AAndIn & BAndIn;  // AND_Gate and_1, 8 bits wide
  assign OrOut = AOrIn | BOrIn;  // OR_Gate or_1, 8 bits wide
  assign NotOut = ~BNotIn;  // NOT_Gate not_1, 8 bits wide
  Shifter shifter_1 (.in(ASlrIn), .\dist (bit_extender_3_out), .out(SlrOut));
  Bit_Extender #(.out_width(3)) bit_extender_3 (.in(BSlrIn), .out(bit_extender_3_out));
  Shifter #(.shift("lr")) shifter_2 (.in(ASrrIn), .\dist (bit_extender_4_out), .out(SrrOut));
  Bit_Extender #(.out_width(3)) bit_extender_4 (.in(BSrrIn), .out(bit_extender_4_out));
  Multiplexer #(.width(8), .enable("false")) multiplexer_2 (
    .in1(BBrzrIn), .out(BrzrOut), .sel(BrzrEscrevePc));  // open: in0
  Multiplexer #(.width(8), .enable("false")) multiplexer_3 (
    .in1(adder_1_out), .out(BrziOut), .sel(BrziEscrevePc));  // open: in0
  Adder adder_4 (.a(BMovhIn), .b(bit_extender_1_out), .out(MovhOut));  // open: cin, cout
  Adder adder_5 (.a(BMovlIn), .b(bit_extender_2_out), .out(MovlOut));  // open: cin, cout
  Multiplexer #(.select(4), .enable("false")) multiplexer_4 (
    .in0(BrzrEscrevePc), .in1(BrziEscrevePc), .in2(1'b1), .in3(1'b1), .in4(1'b0), .in5(1'b0), .in6(1'b0),
    .in7(1'b0), .in8(1'b0), .in9(1'b0), .in10(1'b0), .in11(1'b0), .in12(1'b0), .in13(1'b0), .in14(1'b0),
    .in15(1'b0), .out(EscrevePc), .sel(Funcao));

  // Other names for the same wires on the sheet: JrOut[7:0] = BJrIn; MovrOut[7:0] = BMovrIn; Reg0_30[3:0] = Reg0[3:0];
  //   Reg0_47[3:0] = Reg0[7:4]
endmodule

module memoriaRam (
  input  LeituraMemoria,
  input  EscritaMemoria,
  input  [7:0] Endereco,
  input  [7:0] in_4,
  input  Clock,
  output [7:0] out_6
);

  wire [7:0] ram_1_data;

  RAM ram_1 (.addr(Endereco), .we(EscritaMemoria), .oe(LeituraMemoria), .clk(Clock), .data(ram_1_data));
  Demultiplexer #(.width(8), .enable("false")) demultiplexer_1 (
    .out1(out_6), .in(ram_1_data), .sel(LeituraMemoria));  // open: out0
  Multiplexer #(.width(8), .enable("false")) multiplexer_1 (
    .in1(in_4), .out(ram_1_data), .sel(EscritaMemoria));  // open: in0
endmodule
